# Fritzing sketch knockSensorSketch (saved by Fritzing 0.9.0b)
circuit board: 8.46667cm x 5.64444cm
breadboards: 1

parts:
  Part1 = Arduino Uno (Rev3) - ICSP
  J1 = Piezo Speaker
  LED1 = RGB LED (com. cathode, rgb) [package="5 mm [THT]"]
  J2 = Basic Servo
  R4 = Resistor [tolerance=±5% resistance=10k package="1206 [SMD]"]
  S1 = Pushbutton [package="[SMD]"]
  R1 = Resistor [tolerance=±5% resistance=1M package="1206 [SMD]"]
  R3 = Resistor [tolerance=±5% resistance=560 package="1206 [SMD]"]
  R2 = Resistor [tolerance=±5% resistance=560 package="1206 [SMD]"]

nets:
  N1: Part1.A5/SCL, J1.pin2, R1.Pin_1
  N2: Part1.D12/MISO, R2.Pin_1
  N3: Part1.D13/SCK, R3.Pin_1
  GND: Part1.GND, J1.pin1, LED1.common_cathode, J2.gnd, R4.Pin_0, R1.Pin_0
  N4: Part1.D5_PWM, J2.pulse
  3V3: Part1.3V3, J2.vcc, S1.Pin_3, S1.Pin_4
  N5: LED1.red_anode, R3.Pin_0
  N6: LED1.green_anode, R2.Pin_0
  N7: R4.Pin_1, S1.Pin_1, S1.Pin_2

notes:
  knockSensor
  Servo to open seret drawer
  Piezo for detecting knock pattern
  programming button
  Status LED
